# Fritzing sketch Wemos_cat_feeder (saved by Fritzing 0.9.3b)
circuit board: 8.46667cm x 5.64444cm

parts:
  WeMos_D1_Mini1 = WeMos D1 Mini
  JACK1 = 2.1mm Barrel Jack with Terminal Block
  J1 = Basic Servo

nets:
  5V: WeMos_D1_Mini1.5V, JACK1.POS, J1.vcc
  N1: WeMos_D1_Mini1.D2, J1.pulse
  N2: WeMos_D1_Mini1.G, JACK1.NEG, J1.gnd
